// Logisim project sisdig.circ as structural Verilog: 1 circuit, main circuit main
module main (
);

  wire dipswitch_1_sw3, dipswitch_3_sw3, dipswitch_3_sw5, dipswitch_3_sw7, dipswitch_3_sw9, dipswitch_5_sw1,
       dipswitch_5_sw2, dipswitch_5_sw3, dipswitch_6_sw1, dipswitch_6_sw2, dipswitch_6_sw3, n7400_1_pin1,
       n7400_1_pin2, n7400_1_pin3, n7400_1_pin5, n7400_1_pin6, n7400_1_pin11, n7400_1_pin12, n7402_1_pin1,
       n7402_1_pin2, n7402_1_pin3, n7402_1_pin6, n7402_1_pin7, n7402_1_pin14, n7404_1_pin1, n7404_1_pin2,
       n7404_1_pin3, n7404_1_pin4, n7404_1_pin7, n7404_1_pin14, n7404_2_pin1, n7404_2_pin2, n7404_2_pin7,
       n7404_2_pin14, n7404_3_pin1, n7404_3_pin2, n7404_3_pin3, n7404_3_pin4, n7404_3_pin5, n7404_3_pin6,
       n7404_3_pin7, n7404_3_pin12, n7404_3_pin13, n7404_3_pin14, n7408_1_pin3, n7408_1_pin6, n7408_1_pin7,
       n7408_1_pin8, n7408_1_pin11, n7408_1_pin14, n7408_2_pin3, n7408_2_pin7, n7408_2_pin11, n7408_2_pin14,
       n7411_1_pin6, n7411_1_pin7, n7411_1_pin12, n7411_1_pin14, n7411_2_pin6, n7411_2_pin7, n7411_2_pin12,
       n7411_2_pin14, n7411_3_pin1, n7411_3_pin2, n7411_3_pin3, n7411_3_pin5, n7411_3_pin6, n7411_3_pin7,
       n7411_3_pin12, n7411_3_pin13, n7411_3_pin14, n7421_1_pin6, n7421_1_pin7, n7421_1_pin8, n7421_1_pin14,
       n7421_2_pin6, n7421_2_pin7, n7421_2_pin8, n7421_2_pin14, n7421_3_pin6, n7421_3_pin7, n7421_3_pin8,
       n7421_3_pin14, n7421_4_pin6, n7421_4_pin7, n7421_4_pin8, n7421_4_pin14, n7421_5_pin6, n7421_5_pin7,
       n7421_5_pin8, n7421_5_pin14, n7427_1_pin1, n7427_1_pin4, n7427_1_pin7, n7427_1_pin14, n7432_1_pin1,
       n7432_1_pin2, n7432_1_pin3, n7432_1_pin5, n7432_1_pin6, n7432_1_pin7, n7432_1_pin8, n7432_1_pin9,
       n7432_1_pin12, n7432_1_pin13, n7432_1_pin14, n7432_2_pin3, n7432_2_pin5, n7432_2_pin6, n7432_2_pin7,
       n7432_2_pin14, n7432_3_pin3, n7432_3_pin6, n7432_3_pin7, n7432_3_pin8, n7432_3_pin11, n7432_3_pin14,
       n7432_4_pin3, n7432_4_pin7, n7432_4_pin8, n7432_4_pin11, n7432_4_pin14, n7474_1_pin1, n7474_1_pin2,
       n7474_1_pin3, n7474_1_pin4, n7474_1_pin5, n7474_1_pin6, n7474_1_pin7, n7474_1_pin14;

  _7404 #(.VccGndPorts("true")) u_7404_1 (
    .pin1(n7404_1_pin1), .pin2(n7404_1_pin2), .pin3(n7404_1_pin3), .pin4(n7404_1_pin4), .pin7(n7404_1_pin7),
    .pin14(n7404_1_pin14));  // open: pin5, pin6, pin13, pin12, pin11, pin10, pin9, pin8
  DipSwitch #(.number(3)) dipswitch_1 (.sw1(n7404_1_pin1), .sw2(n7404_1_pin3), .sw3(dipswitch_1_sw3));
  _7404 #(.VccGndPorts("true")) u_7404_2 (
    .pin1(n7404_2_pin1), .pin2(n7404_2_pin2), .pin7(n7404_2_pin7), .pin14(n7404_2_pin14));  // open: pin3, pin4, pin5, pin6, pin13, pin12, pin11, pin10, pin9, pin8
  DipSwitch #(.number(1)) dipswitch_2 (.sw1(n7404_2_pin1));
  _7432 #(.VccGndPorts("true")) u_7432_1 (
    .pin1(n7432_1_pin1), .pin2(n7432_1_pin2), .pin3(n7432_1_pin3), .pin4(n7432_1_pin3), .pin5(n7432_1_pin5),
    .pin6(n7432_1_pin6), .pin7(n7432_1_pin7), .pin14(n7432_1_pin14), .pin13(n7432_1_pin13),
    .pin12(n7432_1_pin12), .pin11(n7432_1_pin5), .pin10(n7432_1_pin6), .pin9(n7432_1_pin9),
    .pin8(n7432_1_pin8));
  DipSwitch #(.number(10)) dipswitch_3 (
    .sw2(n7432_1_pin1), .sw3(dipswitch_3_sw3), .sw4(n7432_1_pin2), .sw5(dipswitch_3_sw5),
    .sw6(n7432_1_pin12), .sw7(dipswitch_3_sw7), .sw8(n7432_1_pin13), .sw9(dipswitch_3_sw9),
    .sw10(n7432_1_pin9));  // open: sw1
  _7404 #(.VccGndPorts("true")) u_7404_3 (
    .pin1(n7404_3_pin1), .pin2(n7404_3_pin2), .pin3(n7404_3_pin3), .pin4(n7404_3_pin4), .pin5(n7404_3_pin5),
    .pin6(n7404_3_pin6), .pin7(n7404_3_pin7), .pin14(n7404_3_pin14), .pin13(n7404_3_pin13),
    .pin12(n7404_3_pin12));  // open: pin11, pin10, pin9, pin8
  DipSwitch #(.number(4)) dipswitch_4 (.sw1(n7404_3_pin13), .sw2(n7404_3_pin1), .sw3(n7404_3_pin3), .sw4(n7404_3_pin5));
  DipSwitch #(.number(3)) dipswitch_5 (.sw1(dipswitch_5_sw1), .sw2(dipswitch_5_sw2), .sw3(dipswitch_5_sw3));
  DipSwitch #(.number(3)) dipswitch_6 (.sw1(dipswitch_6_sw1), .sw2(dipswitch_6_sw2), .sw3(dipswitch_6_sw3));
  _7411 #(.VccGndPorts("true")) u_7411_1 (
    .pin1(dipswitch_1_sw3), .pin2(n7404_1_pin4), .pin3(dipswitch_1_sw3), .pin4(n7404_1_pin2),
    .pin5(n7404_1_pin3), .pin6(n7411_1_pin6), .pin7(n7411_1_pin7), .pin14(n7411_1_pin14),
    .pin13(n7404_1_pin2), .pin12(n7411_1_pin12));  // open: pin11, pin10, pin9, pin8
  _7408 #(.VccGndPorts("true")) u_7408_1 (
    .pin1(n7404_2_pin2), .pin2(dipswitch_5_sw1), .pin3(n7408_1_pin3), .pin4(n7404_2_pin2),
    .pin5(dipswitch_5_sw2), .pin6(n7408_1_pin6), .pin7(n7408_1_pin7), .pin14(n7408_1_pin14),
    .pin13(n7404_2_pin1), .pin12(dipswitch_6_sw1), .pin11(n7408_1_pin11), .pin10(n7404_2_pin1),
    .pin9(dipswitch_6_sw2), .pin8(n7408_1_pin8));
  _7432 #(.VccGndPorts("true")) u_7432_2 (
    .pin1(dipswitch_3_sw3), .pin2(n7432_1_pin2), .pin3(n7432_2_pin3), .pin4(n7432_2_pin3),
    .pin5(n7432_2_pin5), .pin6(n7432_2_pin6), .pin7(n7432_2_pin7), .pin14(n7432_2_pin14),
    .pin13(dipswitch_3_sw7), .pin12(n7432_1_pin13), .pin11(n7432_2_pin5));  // open: pin10, pin9, pin8
  _7421 #(.VccGndPorts("true")) u_7421_1 (
    .pin1(n7404_3_pin12), .pin2(n7404_3_pin2), .pin4(n7404_3_pin4), .pin5(n7404_3_pin6), .pin6(n7421_1_pin6),
    .pin7(n7421_1_pin7), .pin14(n7421_1_pin14), .pin13(n7404_3_pin13), .pin12(n7404_3_pin2),
    .pin10(n7404_3_pin4), .pin9(n7404_3_pin6), .pin8(n7421_1_pin8));  // open: pin3, pin11
  _7411 #(.VccGndPorts("true")) u_7411_2 (
    .pin1(dipswitch_1_sw3), .pin2(n7404_1_pin4), .pin3(dipswitch_1_sw3), .pin4(n7404_1_pin3),
    .pin5(n7404_1_pin1), .pin6(n7411_2_pin6), .pin7(n7411_2_pin7), .pin14(n7411_2_pin14),
    .pin13(n7404_1_pin1), .pin12(n7411_2_pin12));  // open: pin11, pin10, pin9, pin8
  _7408 #(.VccGndPorts("true")) u_7408_2 (
    .pin1(n7404_2_pin2), .pin2(dipswitch_5_sw3), .pin3(n7408_2_pin3), .pin7(n7408_2_pin7),
    .pin14(n7408_2_pin14), .pin13(n7404_2_pin1), .pin12(dipswitch_6_sw3), .pin11(n7408_2_pin11));  // open: pin4, pin5, pin6, pin10, pin9, pin8
  LedBar #(.matrixcols(4)) ledbar_1 (
    .led0(n7411_1_pin12), .led1(n7411_1_pin6), .led2(n7411_2_pin12), .led3(n7411_2_pin6));
  _7432 #(.VccGndPorts("true")) u_7432_3 (
    .pin1(dipswitch_3_sw5), .pin2(n7432_1_pin12), .pin3(n7432_3_pin3), .pin4(dipswitch_3_sw9),
    .pin5(n7432_1_pin9), .pin6(n7432_3_pin6), .pin7(n7432_3_pin7), .pin14(n7432_3_pin14),
    .pin13(n7432_1_pin13), .pin12(n7432_2_pin5), .pin11(n7432_3_pin11), .pin10(n7432_3_pin11),
    .pin9(n7432_3_pin3), .pin8(n7432_3_pin8));
  _7421 #(.VccGndPorts("true")) u_7421_2 (
    .pin1(n7404_3_pin12), .pin2(n7404_3_pin1), .pin4(n7404_3_pin4), .pin5(n7404_3_pin6), .pin6(n7421_2_pin6),
    .pin7(n7421_2_pin7), .pin14(n7421_2_pin14), .pin13(n7404_3_pin13), .pin12(n7404_3_pin1),
    .pin10(n7404_3_pin4), .pin9(n7404_3_pin6), .pin8(n7421_2_pin8));  // open: pin3, pin11
  _7402 #(.VccGndPorts("true")) u_7402_1 (
    .pin1(n7402_1_pin1), .pin2(n7402_1_pin2), .pin3(n7402_1_pin3), .pin4(n7402_1_pin3), .pin5(n7402_1_pin1),
    .pin6(n7402_1_pin6), .pin7(n7402_1_pin7), .pin14(n7402_1_pin14));  // open: pin13, pin12, pin11, pin10, pin9, pin8
  DipSwitch #(.number(2)) dipswitch_7 (.sw1(n7402_1_pin2), .sw2(n7402_1_pin6));
  LedBar #(.matrixcols(3)) ledbar_2 (.led0(n7432_4_pin11), .led1(n7432_4_pin8), .led2(n7432_4_pin3));
  _7432 #(.VccGndPorts("true")) u_7432_4 (
    .pin1(n7408_2_pin3), .pin2(n7408_2_pin11), .pin3(n7432_4_pin3), .pin7(n7432_4_pin7),
    .pin14(n7432_4_pin14), .pin13(n7408_1_pin3), .pin12(n7408_1_pin11), .pin11(n7432_4_pin11),
    .pin10(n7408_1_pin6), .pin9(n7408_1_pin8), .pin8(n7432_4_pin8));  // open: pin4, pin5, pin6
  LedBar #(.matrixcols(4)) ledbar_3 (
    .led0(n7432_1_pin8), .led1(n7432_2_pin6), .led2(n7432_3_pin8), .led3(n7432_3_pin6));
  _7421 #(.VccGndPorts("true")) u_7421_3 (
    .pin1(n7404_3_pin12), .pin2(n7404_3_pin2), .pin4(n7404_3_pin3), .pin5(n7404_3_pin6), .pin6(n7421_3_pin6),
    .pin7(n7421_3_pin7), .pin14(n7421_3_pin14), .pin13(n7404_3_pin13), .pin12(n7404_3_pin2),
    .pin10(n7404_3_pin3), .pin9(n7404_3_pin6), .pin8(n7421_3_pin8));  // open: pin3, pin11
  LedBar #(.matrixcols(2)) ledbar_4 (.led0(n7402_1_pin3), .led1(n7402_1_pin1));
  _7400 u_7400_1 (
    .pin1(n7400_1_pin1), .pin2(n7400_1_pin2), .pin3(n7400_1_pin3), .pin4(n7400_1_pin2), .pin5(n7400_1_pin5),
    .pin6(n7400_1_pin6), .pin13(n7400_1_pin3), .pin12(n7400_1_pin12), .pin11(n7400_1_pin11),
    .pin10(n7400_1_pin11), .pin9(n7400_1_pin6), .pin8(n7400_1_pin12));
  DipSwitch #(.number(2)) dipswitch_8 (.sw1(n7400_1_pin1), .sw2(n7400_1_pin5));
  _7411 #(.ShowInternalStructure("true"), .VccGndPorts("true")) u_7411_3 (
    .pin1(n7411_3_pin1), .pin2(n7411_3_pin2), .pin3(n7411_3_pin3), .pin4(n7411_3_pin2), .pin5(n7411_3_pin5),
    .pin6(n7411_3_pin6), .pin7(n7411_3_pin7), .pin14(n7411_3_pin14), .pin13(n7411_3_pin13),
    .pin12(n7411_3_pin12));  // open: pin11, pin10, pin9, pin8
  DipSwitch #(.number(2)) dipswitch_9 (.sw1(n7411_3_pin1), .sw2(n7411_3_pin5));
  _7421 #(.VccGndPorts("true")) u_7421_4 (
    .pin1(n7404_3_pin12), .pin2(n7404_3_pin1), .pin4(n7404_3_pin3), .pin5(n7404_3_pin6), .pin6(n7421_4_pin6),
    .pin7(n7421_4_pin7), .pin14(n7421_4_pin14), .pin13(n7404_3_pin13), .pin12(n7404_3_pin1),
    .pin10(n7404_3_pin3), .pin9(n7404_3_pin6), .pin8(n7421_4_pin8));  // open: pin3, pin11
  _7474 #(.VccGndPorts("true")) u_7474_1 (
    .pin1(n7474_1_pin1), .pin2(n7474_1_pin2), .pin3(n7474_1_pin3), .pin4(n7474_1_pin4), .pin5(n7474_1_pin5),
    .pin6(n7474_1_pin6), .pin7(n7474_1_pin7), .pin14(n7474_1_pin14));  // open: pin13, pin12, pin11, pin10, pin9, pin8
  Clock clock_1 (.out(n7474_1_pin3));
  DipSwitch #(.number(3)) dipswitch_10 (.sw1(n7474_1_pin1), .sw2(n7474_1_pin2), .sw3(n7474_1_pin4));
  LedBar #(.matrixcols(2)) ledbar_5 (.led0(n7400_1_pin11), .led1(n7400_1_pin12));
  Clock clock_2 (.out(n7400_1_pin2));
  Clock clock_3 (.out(n7411_3_pin2));
  LED led_1 (.in(n7474_1_pin5));
  LED led_2 (.in(n7474_1_pin6));
  _7427 #(.ShowInternalStructure("true"), .VccGndPorts("true")) u_7427_1 (
    .pin1(n7427_1_pin1), .pin2(n7411_3_pin3), .pin3(n7411_3_pin6), .pin4(n7427_1_pin4), .pin5(n7411_3_pin13),
    .pin6(n7411_3_pin3), .pin7(n7427_1_pin7), .pin14(n7427_1_pin14), .pin13(n7411_3_pin12),
    .pin12(n7411_3_pin13));  // open: pin11, pin10, pin9, pin8
  DipSwitch #(.number(2)) dipswitch_11 (.sw1(n7427_1_pin1), .sw2(n7427_1_pin4));
  _7421 #(.VccGndPorts("true")) u_7421_5 (
    .pin1(n7404_3_pin12), .pin2(n7404_3_pin2), .pin4(n7404_3_pin4), .pin5(n7404_3_pin5), .pin6(n7421_5_pin6),
    .pin7(n7421_5_pin7), .pin14(n7421_5_pin14), .pin13(n7404_3_pin13), .pin12(n7404_3_pin2),
    .pin10(n7404_3_pin4), .pin9(n7404_3_pin5), .pin8(n7421_5_pin8));  // open: pin3, pin11
  LedBar #(.matrixcols(2)) ledbar_6 (.led0(n7411_3_pin3), .led1(n7411_3_pin13));
  LedBar #(.matrixcols(10)) ledbar_7 (
    .led0(n7421_1_pin6), .led1(n7421_1_pin8), .led2(n7421_2_pin6), .led3(n7421_2_pin8), .led4(n7421_3_pin6),
    .led5(n7421_3_pin8), .led6(n7421_4_pin6), .led7(n7421_4_pin8), .led8(n7421_5_pin6), .led9(n7421_5_pin8));
  // also tied to GND on the sheet: {n7432_1_pin7, n7404_1_pin7, n7404_3_pin7, n7404_2_pin7, n7411_1_pin7, n7408_1_pin7, n7432_2_pin7, n7421_1_pin7, n7411_2_pin7, n7408_2_pin7, n7421_2_pin7, n7432_3_pin7, n7432_4_pin7, n7402_1_pin7, n7421_3_pin7, n7411_3_pin7, n7421_4_pin7, n7474_1_pin7, n7427_1_pin7, n7421_5_pin7}
  // also tied to VCC on the sheet: {n7432_1_pin14, n7404_1_pin14, n7404_3_pin14, n7404_2_pin14, n7411_1_pin14, n7408_1_pin14, n7432_2_pin14, n7421_1_pin14, n7411_2_pin14, n7408_2_pin14, n7421_2_pin14, n7432_3_pin14, n7432_4_pin14, n7402_1_pin14, n7421_3_pin14, n7411_3_pin14, n7421_4_pin14, n7474_1_pin14, n7427_1_pin14, n7421_5_pin14}

  // Notes on the sheet:
  //   1:4 DEMUX
  //   3-bit 2:1 MUX
  //   Dec-BCD Encoder
  //   SR FF
  //   BCD-Dec Decoder
  //   SR Clocked FF
  //   D FF
  //   JK FF
endmodule
